# Fritzing sketch Zirkulationssteuerung-2 (saved by Fritzing 0.9.6b)
breadboards: 1

parts:
  Bauteil1 = Arduino Uno (Rev3)
  8_Channel_Relay1 = 8 Channel Power Relay
  W1-K = Pushbutton [package=THT]
  W1-B = Pushbutton [package=THT]
  W1-G = Pushbutton [package=THT]
  W2-X = Pushbutton [package=THT]
  W3-B = Pushbutton [package=THT]
  W3-K = Pushbutton [package=THT]
  W1-B-Lü = Pushbutton [package=THT]
  Valve_W1-B = smd LED [color="Red (633nm)" current=0.030 package="0603 [SMD]"]
  W1-B-Valve = Power plug
  W1-K-Valve = Power plug
  W2-Valve = Power plug
  W1-G-Valve = Power plug
  W3-Valve = Power plug
  Power-In-220V_L/N = Power plug
  CircPump = Power plug
  BadLüfter = JST-VHR-3N [part_number=JST-VHR-3N package=THT]
  R2 = Resistor [tolerance=±5% power=0.25 resistance=220 package=THT]
  Valve_W1-B5 = smd LED [color="Red (633nm)" current=0.030 package="0603 [SMD]"]
  R3 = Resistor [tolerance=±5% power=0.25 resistance=220 package=THT]
  Valve_W1-B6 = smd LED [color="Red (633nm)" current=0.030 package="0603 [SMD]"]
  R4 = Resistor [tolerance=±5% power=0.25 resistance=220 package=THT]
  Valve_W1-B7 = smd LED [color="Red (633nm)" current=0.030 package="0603 [SMD]"]
  Valve_W1-B8 = smd LED [color="Red (633nm)" current=0.030 package="0603 [SMD]"]
  Valve_W1-B9 = smd LED [color="Red (633nm)" current=0.030 package="0603 [SMD]"]
  R5 = Resistor [tolerance=±5% power=0.25 resistance=220 package=THT]
  R6 = Resistor [tolerance=±5% power=0.25 resistance=220 package=THT]
  R7 = Resistor [tolerance=±5% power=0.25 resistance=220 package=THT]
  DHT11 = AD22100 - Voltage Output Temperature Sensor with Signal Conditioning [part_number=AD22100]

nets:
  N1: Bauteil1.A0, DHT11.Vo
  N2: Bauteil1.A1, W1-B-Lü.leg1
  N3: Bauteil1.A2, W3-K.leg1
  N4: Bauteil1.A3, W3-B.leg1
  N5: Bauteil1.D8, 8_Channel_Relay1.IN7
  N6: Bauteil1.D9_PWM, 8_Channel_Relay1.IN8
  N7: Bauteil1.D10_PWM/SS, W1-B.leg1
  N8: Bauteil1.D11_PWM/MOSI, W1-K.leg1
  N9: Bauteil1.D12/MISO, W1-G.leg1
  N10: Bauteil1.D13/SCK, W2-X.leg1
  GND: Bauteil1.GND, 8_Channel_Relay1.GND, W1-K.leg0, W1-B.leg0, W1-G.leg0, W2-X.leg0, W3-B.leg0, W3-K.leg0, W1-B-Lü.leg0, W1-B-Valve.GND, W1-K-Valve.GND, W2-Valve.GND, W1-G-Valve.GND, W3-Valve.GND, R2.Pin_0, R3.Pin_0, R4.Pin_0, R5.Pin_0, R6.Pin_0, R7.Pin_0, DHT11.GND
  N11: Bauteil1.D2, 8_Channel_Relay1.IN1
  N12: Bauteil1.D3_PWM, 8_Channel_Relay1.IN2
  N13: Bauteil1.D4, 8_Channel_Relay1.IN3
  N14: Bauteil1.D5_PWM, 8_Channel_Relay1.IN4
  N15: Bauteil1.D6_PWM, 8_Channel_Relay1.IN5
  N16: Bauteil1.D7, 8_Channel_Relay1.IN6
  12V: Bauteil1.VIN
  N17: 8_Channel_Relay1.COM#22, 8_Channel_Relay1.COM#25, 8_Channel_Relay1.COM#28, 8_Channel_Relay1.COM#31, 8_Channel_Relay1.COM#34, DHT11.V+
  N18: 8_Channel_Relay1.NO#23, Valve_W1-B.anode, W1-B-Valve.VCC
  N19: 8_Channel_Relay1.NO#26, W1-K-Valve.VCC, Valve_W1-B5.anode
  N20: 8_Channel_Relay1.NO#29, W1-G-Valve.VCC, Valve_W1-B6.anode
  N21: 8_Channel_Relay1.NO#32, W2-Valve.VCC, Valve_W1-B7.anode
  N22: 8_Channel_Relay1.NO#35, W3-Valve.VCC, Valve_W1-B8.anode, Valve_W1-B9.anode
  N23: 8_Channel_Relay1.COM#37, 8_Channel_Relay1.COM#43, Power-In-220V_L/N.VCC
  N24: 8_Channel_Relay1.NO#38, CircPump.VCC
  N25: 8_Channel_Relay1.NC, BadLüfter.pin3, BadLüfter.pin_6
  N26: 8_Channel_Relay1.COM#40, 8_Channel_Relay1.NO#44
  N27: 8_Channel_Relay1.NO#41, BadLüfter.pin2, BadLüfter.pin_5
  N28: Valve_W1-B.cathode, R2.Pin_1
  GND_2: Power-In-220V_L/N.GND, CircPump.GND, BadLüfter.pin1, BadLüfter.pin_4
  N29: Valve_W1-B5.cathode, R3.Pin_1
  N30: Valve_W1-B6.cathode, R4.Pin_1
  N31: Valve_W1-B7.cathode, R5.Pin_1
  N32: Valve_W1-B8.cathode, R7.Pin_1
  N33: Valve_W1-B9.cathode, R6.Pin_1

custom parts:
  8 Channel Power Relay: An 8 channel power relay. The module operates at 5V.
